# Fritzing sketch final-circuit (saved by Fritzing 0.9.2b)
breadboards: 1

parts:
  Parte1 = Arduino Uno (Rev3)
  LCD1 = LCD screen
  R1 = Trimmer Potentiometer [maximum_resistance=10kΩ package=THT]
  T1 = LM35 Temperature Sensor [package="TO92 [THT]"]
  RHT1 = Humidity and Temperature Sensor RHT03

nets:
  N1: Parte1.A0, T1.Vout
  N2: Parte1.D8, LCD1.DB3
  N3: Parte1.D9_PWM, LCD1.DB4
  N4: Parte1.D10_PWM/SS, LCD1.DB5
  N5: Parte1.D11_PWM/MOSI, LCD1.DB6
  N6: Parte1.D12/MISO, LCD1.DB7
  N7: Parte1.D13/SCK, RHT1.Data-signal
  N8: Parte1.D2, LCD1.RS
  N9: Parte1.D3_PWM, LCD1.R/W
  N10: Parte1.D4, LCD1.E
  N11: Parte1.D5_PWM, LCD1.DB0
  N12: Parte1.D6_PWM, LCD1.DB1
  N13: Parte1.D7, LCD1.DB2
  5V: Parte1.5V, LCD1.VDD, R1.leg1, T1.+Vs, RHT1.Vcc
  GND: Parte1.GND, LCD1.VSS, R1.leg2, T1.GND, RHT1.GND_2
  N14: LCD1.V0, R1.wiper
